// Logisim project 3 bit adder.circ as structural Verilog: 1 circuit, main circuit adder/subtractor
module adder_subtractor (
  input  ao,
  input  bo,
  input  controller,
  input  a1,
  input  b1,
  input  a2,
  input  b2,
  output LSB,
  output s1,
  output s2
);

  wire main_1_carry, main_2_carry, n7486_1_p3, n7486_1_p6, n7486_1_p9, n7486_1_p10;

  // _7486 7486_1: pin names not known; wires that end beside it: bo, controller, n7486_1_p3, b1, controller, n7486_1_p6, b2, controller, n7486_1_p9, n7486_1_p10
  FullAdder_main main_1 (.b(n7486_1_p3), .a(ao), .carry(main_1_carry), .sum(LSB), .cin(controller));
  FullAdder_main main_2 (.b(n7486_1_p6), .a(a1), .carry(main_2_carry), .sum(s1), .cin(main_1_carry));
  FullAdder_main main_3 (.b(n7486_1_p9), .a(a2), .carry(n7486_1_p10), .sum(s2), .cin(main_2_carry));
endmodule
