// Logisim project ADD3.circ as structural Verilog: 1 circuit, main circuit ADD3 
module ADD3 (
  input  A3,
  input  A2,
  input  A1,
  input  A0,
  output W,
  output X,
  output Y,
  output Z
);

  wire A0_t, A1_t, A2_t, A3_t, n7408_1__3__1y, n7408_1__6__2y, n7408_1__8__3y, n7408_1__11__4y,
       n7408_2__3__1y, n7408_2__6__2y, n7408_3__3__1y, n7408_3__6__2y, n7408_3__11__4y, n7408_4__3__1y,
       n7408_4__8__3y, n7408_4__11__4y, n7432_1__3__1y, n7432_1__11__4y, n7432_2__11__4y;

  _7404 u_7404_1 (
    ._1__1A(A0), ._2__1Y(A0_t), ._3__2A(A1), ._4__2Y(A1_t), ._13__6A(A2), ._12__6Y(A2_t), ._11__5A(A3),
    ._10__5Y(A3_t));  // open: _5__3A, _6__3Y, _7__GND, _14__Vcc, _9__4A, _8__4Y
  _7408 u_7408_1 (
    ._1__1A(n7432_1__3__1y), ._2__1B(A2), ._3__1Y(n7408_1__3__1y), ._4__2A(A1_t), ._5__2B(A0_t),
    ._6__2Y(n7408_1__6__2y), ._13__4B(A0), ._12__4A(A1), ._11__4Y(n7408_1__11__4y), ._10__3B(A2),
    ._9__3A(n7408_1__6__2y), ._8__3Y(n7408_1__8__3y));  // open: _7__GND, _14__Vcc
  _7432 u_7432_1 (
    ._1__1A(A0), ._2__1B(A1), ._3__1Y(n7432_1__3__1y), ._4__2A(n7408_1__3__1y), ._5__2B(A3), ._6__2Y(W),
    ._13__4B(n7408_3__6__2y), ._12__4A(n7408_1__11__4y), ._11__4Y(n7432_1__11__4y),
    ._10__3B(n7432_1__11__4y), ._9__3A(n7408_3__3__1y), ._8__3Y(Y));  // open: _7__GND, _14__Vcc
  _7408 u_7408_2 (
    ._1__1A(A2), ._2__1B(A1), ._3__1Y(n7408_2__3__1y), ._4__2A(n7408_2__3__1y), ._5__2B(A0_t),
    ._6__2Y(n7408_2__6__2y));  // open: _7__GND, _14__Vcc, _13__4B, _12__4A, _11__4Y, _10__3B, _9__3A, _8__3Y
  _7432 u_7432_2 (
    ._1__1A(n7408_3__11__4y), ._2__1B(n7408_1__8__3y), ._3__1Y(X), ._13__4B(n7408_4__3__1y),
    ._12__4A(n7408_4__8__3y), ._11__4Y(n7432_2__11__4y), ._10__3B(n7432_2__11__4y), ._9__3A(n7408_2__6__2y),
    ._8__3Y(Z));  // open: _4__2A, _5__2B, _6__2Y, _7__GND, _14__Vcc
  _7408 u_7408_3 (
    ._1__1A(A0_t), ._2__1B(A3), ._3__1Y(n7408_3__3__1y), ._4__2A(A2_t), ._5__2B(A1), ._6__2Y(n7408_3__6__2y),
    ._13__4B(A0), ._12__4A(A3), ._11__4Y(n7408_3__11__4y));  // open: _7__GND, _14__Vcc, _10__3B, _9__3A, _8__3Y
  _7408 u_7408_4 (
    ._1__1A(A3), ._2__1B(A0_t), ._3__1Y(n7408_4__3__1y), ._13__4B(A3_t), ._12__4A(A2_t),
    ._11__4Y(n7408_4__11__4y), ._10__3B(n7408_4__11__4y), ._9__3A(A0), ._8__3Y(n7408_4__8__3y));  // open: _4__2A, _5__2B, _6__2Y, _7__GND, _14__Vcc
endmodule
