// Logisim project ALU.circ as structural Verilog: 1 circuit, main circuit ALU
module ALU (
  input  sign1,
  input  a0,
  input  a1,
  input  a2,
  input  sign2,
  input  b0,
  input  b1,
  input  b2,
  input  O,
  input  P,
  output S0,
  output S1,
  output S2,
  output S3,
  output mult_zero_flag,
  output add_sub_zero_flag,
  output out_17,
  output S4,
  output S5,
  output sign
);

  wire a_s_O0, a_s_O1, a_s_O2, a_s_O3, a_s_sign, mult_O0, mult_O1, mult_O2, mult_O3, mult_O4, mult_O5,
       mult_sign, n7432_1__3__1y, n7432_1__6__2y, n7432_1__8__3y, n7432_2__3__1y, n7432_2__6__2y,
       n7432_2__8__3y, n7432_2__11__4y, n7432_3__3__1y, rem_O0, rem_O1, rem_O2, sign_t;

  Final_Adder_subtracor final_adder_subtracor_1 (
    .A3(sign1), .A2(a2), .A1(a1), .A0(a0), .B3(sign2), .B2(b2), .B1(b1), .B0(b0), .O(O), .P(P),
    .Sign(a_s_sign), .S3(a_s_O3), .S2(a_s_O2), .S1(a_s_O1), .S0(a_s_O0));
  Multiplier multiplier_1 (
    .A0(a0), .B0(b0), .A1(a1), .B1(b1), .A2(a2), .B2(b2), .A3(sign1), .B3(sign2), .O1(mult_O0), .O2(mult_O1),
    .O3(mult_O2), .O4(mult_O3), .O5(mult_O4), .O6(mult_O5), .O7(mult_sign));
  // REM rem_1: pin names not known; wires that end beside it: b0, b1, b2, a0, a1, a2, sign1, sign_t, rem_O2, rem_O1, rem_O0, out_17
  _7432 u_7432_1 (
    ._1__1A(a_s_O0), ._2__1B(a_s_O1), ._3__1Y(n7432_1__3__1y), ._4__2A(n7432_1__3__1y), ._5__2B(a_s_O2),
    ._6__2Y(n7432_1__6__2y), ._7__GND(1'b0), ._14__Vcc(1'b1), ._10__3B(a_s_O3), ._9__3A(n7432_1__6__2y),
    ._8__3Y(n7432_1__8__3y));  // open: _13__4B, _12__4A, _11__4Y
  _7404 u_7404_1 (
    ._3__2A(n7432_1__8__3y), ._4__2Y(add_sub_zero_flag), ._9__4A(n7432_3__3__1y), ._8__4Y(mult_zero_flag));  // open: _1__1A, _2__1Y, _5__3A, _6__3Y, _7__GND, _14__Vcc, _13__6A, _12__6Y, _11__5A, _10__5Y
  _7432 u_7432_2 (
    ._1__1A(mult_O0), ._2__1B(mult_O1), ._3__1Y(n7432_2__3__1y), ._4__2A(n7432_2__3__1y), ._5__2B(mult_O2),
    ._6__2Y(n7432_2__6__2y), ._13__4B(mult_O4), ._12__4A(n7432_2__8__3y), ._11__4Y(n7432_2__11__4y),
    ._10__3B(mult_O3), ._9__3A(n7432_2__6__2y), ._8__3Y(n7432_2__8__3y));  // open: _7__GND, _14__Vcc
  _7432 u_7432_3 (
    ._1__1A(n7432_2__11__4y), ._2__1B(mult_O5), ._3__1Y(n7432_3__3__1y));  // open: _4__2A, _5__2B, _6__2Y, _7__GND, _14__Vcc, _13__4B, _12__4A, _11__4Y, _10__3B, _9__3A, _8__3Y
  _74153 u_74153_1 (
    ._2__B(O), ._3__1C3(rem_O0), ._4__1C2(mult_O0), ._5__1C1(a_s_O0), ._6__1C0(a_s_O0), ._7__Y1(S0),
    ._8__GND(1'b0), ._16__Vcc(1'b1), ._14__A(P), ._13__2C3(rem_O1), ._12__2C2(mult_O1), ._11__2C1(a_s_O1),
    ._10__2C0(a_s_O1), ._9__Y2(S1));
  _74153 u_74153_2 (
    ._2__B(O), ._3__1C3(rem_O2), ._4__1C2(mult_O2), ._5__1C1(a_s_O2), ._6__1C0(a_s_O2), ._7__Y1(S2),
    ._8__GND(1'b0), ._16__Vcc(1'b1), ._14__A(P), ._13__2C3(1'b0), ._12__2C2(mult_O3), ._11__2C1(a_s_O3),
    ._10__2C0(a_s_O3), ._9__Y2(S3));
  _74153 u_74153_3 (
    ._2__B(O), ._3__1C3(1'b0), ._4__1C2(mult_O4), ._5__1C1(1'b0), ._6__1C0(1'b0), ._7__Y1(S4),
    ._8__GND(1'b0), ._16__Vcc(1'b1), ._14__A(P), ._13__2C3(1'b0), ._12__2C2(mult_O5), ._11__2C1(1'b0),
    ._10__2C0(1'b0), ._9__Y2(S5));
  _74153 u_74153_4 (
    ._2__B(O), ._3__1C3(1'b0), ._4__1C2(mult_sign), ._5__1C1(a_s_sign), ._6__1C0(a_s_sign), ._7__Y1(sign),
    ._8__GND(1'b0), ._16__Vcc(1'b1), ._14__A(P));  // open: _13__2C3, _12__2C2, _11__2C1, _10__2C0, _9__Y2

  // Other names for the same wires on the sheet: sign_2 = sign2
endmodule
