// Logisim project BCD to 7 segment.circ as structural Verilog: 1 circuit, main circuit BCD to 7 segment
module BCD_to_7_segment (
  input  sign,
  input  a5,
  input  a4,
  input  a3,
  input  a2,
  input  a1,
  input  a0,
  output sign_2,
  output gt,
  output at,
  output bt,
  output ft,
  output gu,
  output fu,
  output au,
  output bu,
  output ct,
  output dt,
  output et,
  output eu,
  output du,
  output cu
);

  wire binary_to_bcd_1_b0, binary_to_bcd_1_b1, binary_to_bcd_1_b2, binary_to_bcd_1_b3, binary_to_bcd_1_c0,
       binary_to_bcd_1_c1, binary_to_bcd_1_c2, binary_to_bcd_1_c3;

  _7448 u_7448_1 (
    ._1__B(1'b0), ._2__C(1'b0), ._3__nLT(1'b1), ._4__NC(1'b1), ._5__nRBI(1'b1), ._6__D(sign), ._7__A(1'b0),
    ._8__GND(1'b0), ._16__Vcc(1'b1), ._14__g(sign_2));  // open: _15__f, _13__a, _12__b, _11__c, _10__d, _9__e
  _7448 u_7448_2 (
    ._1__B(binary_to_bcd_1_c1), ._2__C(binary_to_bcd_1_c2), ._3__nLT(1'b1), ._4__NC(1'b1), ._5__nRBI(1'b1),
    ._6__D(binary_to_bcd_1_c3), ._7__A(binary_to_bcd_1_c0), ._8__GND(1'b0), ._16__Vcc(1'b1), ._15__f(ft),
    ._14__g(gt), ._13__a(at), ._12__b(bt), ._11__c(ct), ._10__d(dt), ._9__e(et));
  Binary_to_BCD binary_to_bcd_1 (
    .a5(a5), .a4(a4), .a3(a3), .a2(a2), .a1(a1), .a0(a0), .c3(binary_to_bcd_1_c3), .c2(binary_to_bcd_1_c2),
    .c1(binary_to_bcd_1_c1), .c0(binary_to_bcd_1_c0), .b3(binary_to_bcd_1_b3), .b2(binary_to_bcd_1_b2),
    .b1(binary_to_bcd_1_b1), .b0(binary_to_bcd_1_b0));
  _7448 u_7448_3 (
    ._1__B(binary_to_bcd_1_b1), ._2__C(binary_to_bcd_1_b2), ._3__nLT(1'b1), ._4__NC(1'b1), ._5__nRBI(1'b1),
    ._6__D(binary_to_bcd_1_b3), ._7__A(binary_to_bcd_1_b0), ._8__GND(1'b0), ._16__Vcc(1'b1), ._15__f(fu),
    ._14__g(gu), ._13__a(au), ._12__b(bu), ._11__c(cu), ._10__d(du), ._9__e(eu));
endmodule
