// Logisim project Binary to 7 segment.circ as structural Verilog: 1 circuit, main circuit BCD to 7 segment
module BCD_to_7_segment (
  input  sign,
  input  a5,
  input  a4,
  input  a3,
  input  a2,
  input  a1,
  input  a0
);

  wire main_1_p1, main_1_p3, main_1_p5, main_1_p7, main_1_p9, main_1_p11, main_1_p13, main_1_p14, n7448_1_p7,
       n7448_2__9__e, n7448_2__10__d, n7448_2__11__c, n7448_2__12__b, n7448_2__13__a, n7448_2__14__g,
       n7448_2__15__f, n7448_3_p2, n7448_3_p4, n7448_3_p6, n7448_3_p8, n7448_3_p10, n7448_3_p12, n7448_3_p14;

  _7_Segment_Display u_7_segment_display_1 (.g(n7448_1_p7));  // open: f, a, b, e, d, c, dp
  // _7448 7448_1: pin names not known; wires that end beside it: 1'b0, 1'b0, sign, 1'b1, 1'b1, 1'b1, n7448_1_p7, 1'b0, 1'b0, 1'b1
  _7448 u_7448_2 (
    ._1__B(main_1_p5), ._2__C(main_1_p3), ._3__nLT(1'b1), ._4__NC(1'b1), ._5__nRBI(1'b1), ._6__D(main_1_p1),
    ._7__A(main_1_p7), ._8__GND(1'b0), ._16__Vcc(1'b1), ._15__f(n7448_2__15__f), ._14__g(n7448_2__14__g),
    ._13__a(n7448_2__13__a), ._12__b(n7448_2__12__b), ._11__c(n7448_2__11__c), ._10__d(n7448_2__10__d),
    ._9__e(n7448_2__9__e));
  _7_Segment_Display u_7_segment_display_2 (
    .g(n7448_2__14__g), .f(n7448_2__15__f), .a(n7448_2__13__a), .b(n7448_2__12__b), .e(n7448_2__9__e),
    .d(n7448_2__10__d), .c(n7448_2__11__c));  // open: dp
  // Binary_to_BCD_main main_1: pin names not known; wires that end beside it: main_1_p1, a5, main_1_p3, a4, main_1_p5, a3, main_1_p7, a2, main_1_p9, a1, main_1_p11, a0, main_1_p13, main_1_p14
  _7_Segment_Display u_7_segment_display_3 (
    .g(n7448_3_p12), .f(n7448_3_p14), .a(n7448_3_p10), .b(n7448_3_p8), .e(n7448_3_p2), .d(n7448_3_p4),
    .c(n7448_3_p6));  // open: dp
  // _7448 7448_3: pin names not known; wires that end beside it: 1'b0, n7448_3_p2, main_1_p14, n7448_3_p4, main_1_p9, n7448_3_p6, 1'b1, n7448_3_p8, 1'b1, n7448_3_p10, 1'b1, n7448_3_p12, main_1_p11, n7448_3_p14, main_1_p13, 1'b1
endmodule
