// Logisim project Final final aaadder.circ as structural Verilog: 5 circuits, main circuit main
module main (
  input  A3,
  input  A2,
  input  A1,
  input  A0,
  input  B3,
  input  B2,
  input  B1,
  input  B0,
  input  O,
  input  P,
  output Sign,
  output S3,
  output S2,
  output S1,
  output S0
);

  wire B_Sub, full_adder_1_sum, main_1_carry, main_1_sum, main_2_carry, main_2_sum, main_3_carry, main_3_sum,
       n2_s_comp_1_out_5, n2_s_comp_1_out_6, n2_s_comp_1_out_7, n2_s_comp_1_out_8, n7404_1__2__1y,
       n7404_1__4__2y, n7404_1__10__5y, n7404_1__12__6y, n7408_1__3__1y, n7408_1__8__3y, n7408_1__11__4y,
       n7408_2__3__1y, n7486_1__11__4y, n7486_2__3__1y, n7486_2__6__2y, Result;

  _7486 u_7486_1 (
    ._13__4B(A3), ._12__4A(Result), ._11__4Y(n7486_1__11__4y));  // open: _1__1A, _2__1B, _3__1Y, _4__2A, _5__2B, _6__2Y, _7__GND, _14__Vcc, _10__3B, _9__3A, _8__3Y
  _7432 u_7432_1 (
    ._13__4B(n7408_1__3__1y), ._12__4A(n7408_1__8__3y), ._11__4Y(Sign));  // open: _1__1A, _2__1B, _3__1Y, _4__2A, _5__2B, _6__2Y, _7__GND, _14__Vcc, _10__3B, _9__3A, _8__3Y
  _7404 u_7404_1 (
    ._1__1A(Result), ._2__1Y(n7404_1__2__1y), ._3__2A(n7486_1__11__4y), ._4__2Y(n7404_1__4__2y),
    ._13__6A(A3), ._12__6Y(n7404_1__12__6y), ._11__5A(full_adder_1_sum), ._10__5Y(n7404_1__10__5y));  // open: _5__3A, _6__3Y, _7__GND, _14__Vcc, _9__4A, _8__4Y
  _7408 u_7408_1 (
    ._1__1A(n7404_1__10__5y), ._2__1B(n7486_1__11__4y), ._3__1Y(n7408_1__3__1y), ._4__2A(n7404_1__4__2y),
    ._5__2B(full_adder_1_sum), ._6__2Y(S3), ._13__4B(n7404_1__2__1y), ._12__4A(A3),
    ._11__4Y(n7408_1__11__4y), ._10__3B(Result), ._9__3A(A3), ._8__3Y(n7408_1__8__3y));  // open: _7__GND, _14__Vcc
  Full_Adder full_adder_1 (.A(n2_s_comp_1_out_5), .B(main_1_carry), .Sum(full_adder_1_sum), .Cin(1'b0));  // open: Cout
  _2_s_Comp u_2_s_comp_1 (
    .in_1(A2), .in_2(A1), .in_3(A0), .out_5(n2_s_comp_1_out_5), .out_6(n2_s_comp_1_out_6),
    .out_7(n2_s_comp_1_out_7), .out_8(n2_s_comp_1_out_8), .Cin(n7408_1__11__4y));
  FullAdder_main main_1 (.b(n2_s_comp_1_out_6), .a(B_Sub), .carry(main_1_carry), .sum(main_1_sum), .cin(main_2_carry));
  FullAdder_main main_2 (
    .b(n2_s_comp_1_out_7), .a(n7486_2__6__2y), .carry(main_2_carry), .sum(main_2_sum), .cin(main_3_carry));
  _2_s_Comp u_2_s_comp_2 (
    .in_1(main_1_sum), .in_2(main_2_sum), .in_3(main_3_sum), .out_6(S2), .out_7(S1), .out_8(S0),
    .Cin(n7408_1__3__1y));  // open: out_5
  FullAdder_main main_3 (
    .b(n2_s_comp_1_out_8), .a(n7486_2__3__1y), .carry(main_3_carry), .sum(main_3_sum), .cin(n7408_2__3__1y));
  _7486 u_7486_2 (
    ._1__1A(n7408_2__3__1y), ._2__1B(B0), ._3__1Y(n7486_2__3__1y), ._4__2A(n7408_2__3__1y), ._5__2B(B1),
    ._6__2Y(n7486_2__6__2y), ._13__4B(B3), ._12__4A(P), ._11__4Y(Result), ._10__3B(B2),
    ._9__3A(n7408_2__3__1y), ._8__3Y(B_Sub));  // open: _7__GND, _14__Vcc
  _7408 u_7408_2 (
    ._1__1A(n7404_1__12__6y), ._2__1B(Result), ._3__1Y(n7408_2__3__1y));  // open: _4__2A, _5__2B, _6__2Y, _7__GND, _14__Vcc, _13__4B, _12__4A, _11__4Y, _10__3B, _9__3A, _8__3Y
endmodule

module Full_Adder (
  input  A,
  input  B,
  input  Cin,
  output Cout,
  output Sum
);

  wire n7408_1__3__1y, n7408_1__8__3y, n7408_1__11__4y, n7432_1__11__4y, n7486_1__3__1y;

  _7408 u_7408_1 (
    ._1__1A(B), ._2__1B(Cin), ._3__1Y(n7408_1__3__1y), ._13__4B(A), ._12__4A(B), ._11__4Y(n7408_1__11__4y),
    ._10__3B(A), ._9__3A(Cin), ._8__3Y(n7408_1__8__3y));  // open: _4__2A, _5__2B, _6__2Y, _7__GND, _14__Vcc
  _7432 u_7432_1 (
    ._13__4B(n7408_1__8__3y), ._12__4A(n7408_1__11__4y), ._11__4Y(n7432_1__11__4y),
    ._10__3B(n7432_1__11__4y), ._9__3A(n7408_1__3__1y), ._8__3Y(Cout));  // open: _1__1A, _2__1B, _3__1Y, _4__2A, _5__2B, _6__2Y, _7__GND, _14__Vcc
  _7486 u_7486_1 (
    ._1__1A(B), ._2__1B(Cin), ._3__1Y(n7486_1__3__1y), ._4__2A(n7486_1__3__1y), ._5__2B(A), ._6__2Y(Sum));  // open: _7__GND, _14__Vcc, _13__4B, _12__4A, _11__4Y, _10__3B, _9__3A, _8__3Y
endmodule

module _2_s_Comp (
  input  in_1,
  input  in_2,
  input  in_3,
  input  Cin,
  output out_5,
  output out_6,
  output out_7,
  output out_8
);

  wire full_adder_2_cout, full_adder_3_cout, n7486_1__3__1y, n7486_1__6__2y, n7486_1__11__4y;

  Full_Adder full_adder_1 (.A(1'b0), .B(n7486_1__11__4y), .Cout(out_5), .Sum(out_6), .Cin(full_adder_2_cout));
  Full_Adder full_adder_2 (
    .A(1'b0), .B(n7486_1__6__2y), .Cout(full_adder_2_cout), .Sum(out_7), .Cin(full_adder_3_cout));
  Full_Adder full_adder_3 (.A(1'b0), .B(n7486_1__3__1y), .Cout(full_adder_3_cout), .Sum(out_8), .Cin(Cin));
  _7486 u_7486_1 (
    ._1__1A(in_3), ._2__1B(Cin), ._3__1Y(n7486_1__3__1y), ._4__2A(Cin), ._5__2B(in_2),
    ._6__2Y(n7486_1__6__2y), ._13__4B(in_1), ._12__4A(Cin), ._11__4Y(n7486_1__11__4y));  // open: _7__GND, _14__Vcc, _10__3B, _9__3A, _8__3Y
endmodule

module REM (
  input  B0,
  input  B1,
  input  B2,
  input  B3,
  input  A0,
  input  A1,
  input  A2,
  input  A3,
  output out_9,
  output S3,
  output S2,
  output S1,
  output S0
);

  wire n7402_1__1__1y, n7404_1__10__5y, n7404_1__12__6y, n7408_1__3__1y, n7432_1__3__1y, n7432_1__6__2y,
       n7432_2__3__1y, n74157_1__4__y1, n74157_1__7__y2, n74157_2__4__y1, n74157_2__7__y2, n74157_3__4__y1,
       n74157_3__7__y2, n74157_4__4__y1, n74157_4__7__y2, n74157_5__4__y1, n74157_5__7__y2, rem2_s_1_out_8,
       rem2_s_1_out_9, rem2_s_1_out_10, rem2_s_1_out_11, rem2_s_2_out_8, rem2_s_2_out_9, rem2_s_2_out_10,
       rem2_s_2_out_11, rem2_s_3_out_8, rem2_s_3_out_9, rem2_s_3_out_10, rem2_s_3_out_11, rem2_s_4_out_8,
       rem2_s_4_out_9, rem2_s_4_out_10, rem2_s_4_out_11, ss, undriven, undriven_2, undriven_3, undriven_4,
       undriven_5;
  wire [2:2] n74157_6__12__y4;

  _7432 u_7432_1 (
    ._1__1A(B0), ._2__1B(B1), ._3__1Y(n7432_1__3__1y), ._4__2A(n7432_1__3__1y), ._5__2B(B2),
    ._6__2Y(n7432_1__6__2y));  // open: _7__GND, _14__Vcc, _13__4B, _12__4A, _11__4Y, _10__3B, _9__3A, _8__3Y
  REM2_s rem2_s_1 (
    .A2(A2), .A1(A1), .A0(A0), .B2(B2), .B1(B1), .B0(B0), .out_8(rem2_s_1_out_8), .out_9(rem2_s_1_out_9),
    .out_10(rem2_s_1_out_10), .out_11(rem2_s_1_out_11), .Cin(1'b1));
  REM2_s rem2_s_2 (
    .A2(undriven), .A1(n74157_1__7__y2), .A0(n74157_1__4__y1), .B2(B2), .B1(B1), .B0(B0),
    .out_8(rem2_s_2_out_8), .out_9(rem2_s_2_out_9), .out_10(rem2_s_2_out_10), .out_11(rem2_s_2_out_11),
    .Cin(1'b1));
  _7404 u_7404_1 (
    ._1__1A(n7432_1__6__2y), ._2__1Y(out_9), ._13__6A(ss), ._12__6Y(n7404_1__12__6y),
    ._11__5A(n7404_1__12__6y), ._10__5Y(n7404_1__10__5y));  // open: _3__2A, _4__2Y, _5__3A, _6__3Y, _7__GND, _14__Vcc, _9__4A, _8__4Y
  _74157 u_74157_1 (
    ._1__S(rem2_s_1_out_8), ._2__A1(A0), ._3__B1(rem2_s_1_out_11), ._4__Y1(n74157_1__4__y1), ._5__A2(A1),
    ._6__B2(rem2_s_1_out_10), ._7__Y2(n74157_1__7__y2), ._14__A4(1'b0), ._13__B4(A2),
    ._12__Y4(rem2_s_1_out_9), ._11__A3(undriven));  // open: _8__GND, _16__Vcc, _10__B3, _9__Y3
  _74157 u_74157_2 (
    ._1__S(rem2_s_2_out_8), ._2__A1(n74157_1__4__y1), ._3__B1(rem2_s_2_out_11), ._4__Y1(n74157_2__4__y1),
    ._5__A2(n74157_1__7__y2), ._6__B2(rem2_s_2_out_10), ._7__Y2(n74157_2__7__y2), ._14__A4(1'b0),
    ._13__B4(undriven), ._12__Y4(rem2_s_2_out_9), ._11__A3(undriven_2));  // open: _8__GND, _16__Vcc, _10__B3, _9__Y3
  REM2_s rem2_s_3 (
    .A2(undriven_2), .A1(n74157_2__7__y2), .A0(n74157_2__4__y1), .B2(B2), .B1(B1), .B0(B0),
    .out_8(rem2_s_3_out_8), .out_9(rem2_s_3_out_9), .out_10(rem2_s_3_out_10), .out_11(rem2_s_3_out_11),
    .Cin(1'b1));
  _74157 u_74157_3 (
    ._1__S(rem2_s_3_out_8), ._2__A1(n74157_2__4__y1), ._3__B1(rem2_s_3_out_11), ._4__Y1(n74157_3__4__y1),
    ._5__A2(n74157_2__7__y2), ._6__B2(rem2_s_3_out_10), ._7__Y2(n74157_3__7__y2), ._14__A4(1'b0),
    ._13__B4(undriven_2), ._12__Y4(rem2_s_3_out_9), ._11__A3(undriven_4));  // open: _8__GND, _16__Vcc, _10__B3, _9__Y3
  REM2_s rem2_s_4 (
    .A2(undriven_4), .A1(n74157_3__7__y2), .A0(n74157_3__4__y1), .B2(B2), .B1(B1), .B0(B0),
    .out_8(rem2_s_4_out_8), .out_9(rem2_s_4_out_9), .out_10(rem2_s_4_out_10), .out_11(rem2_s_4_out_11),
    .Cin(1'b1));
  _74157 u_74157_4 (
    ._1__S(rem2_s_4_out_8), ._2__A1(n74157_3__4__y1), ._3__B1(rem2_s_4_out_11), ._4__Y1(n74157_4__4__y1),
    ._5__A2(n74157_3__7__y2), ._6__B2(rem2_s_4_out_10), ._7__Y2(n74157_4__7__y2), ._14__A4(1'b0),
    ._13__B4(undriven_4), ._12__Y4(rem2_s_4_out_9), ._11__A3(undriven_3));  // open: _8__GND, _16__Vcc, _10__B3, _9__Y3
  _74157 u_74157_5 (
    ._1__S(out_9), ._2__A1(n74157_4__4__y1), ._3__B1(B0), ._4__Y1(n74157_5__4__y1), ._5__A2(n74157_4__7__y2),
    ._6__B2(B1), ._7__Y2(n74157_5__7__y2), ._14__A4(1'b0), ._13__B4(undriven_3), ._12__Y4(B2),
    ._11__A3(undriven_5));  // open: _8__GND, _16__Vcc, _10__B3, _9__Y3
  _7402 u_7402_1 (
    ._1__1Y(n7402_1__1__1y), ._2__1A(B1), ._3__1B(B2));  // open: _4__2Y, _5__2A, _6__2B, _7__GND, _14__Vcc, _13__4Y, _12__4B, _11__4A, _10__3Y, _9__3B, _8__3A
  _7408 u_7408_1 (
    ._1__1A(n7402_1__1__1y), ._2__1B(B0), ._3__1Y(n7408_1__3__1y), ._13__4B(n7404_1__10__5y), ._12__4A(A3),
    ._11__4Y(S3));  // open: _4__2A, _5__2B, _6__2Y, _7__GND, _14__Vcc, _10__3B, _9__3A, _8__3Y
  _74157 u_74157_6 (
    ._1__S(n7408_1__3__1y), ._2__A1(n74157_5__4__y1), ._3__B1(1'b0), ._4__Y1(S0), ._5__A2(n74157_5__7__y2),
    ._6__B2(1'b0), ._7__Y2(S1), ._14__A4(1'b0), ._13__B4(undriven_5), ._12__Y4(n74157_6__12__y4[2]),
    ._11__A3(S2));  // open: _8__GND, _16__Vcc, _10__B3, _9__Y3
  _7432 u_7432_2 (
    ._1__1A(S1), ._2__1B(S0), ._3__1Y(n7432_2__3__1y), ._4__2A(n7432_2__3__1y), ._5__2B(S2), ._6__2Y(ss));  // open: _7__GND, _14__Vcc, _13__4B, _12__4A, _11__4Y, _10__3B, _9__3A, _8__3Y
  // also tied to GND on the sheet: n74157_6__12__y4[2]

  // Other names for the same wires on the sheet: Sign_bit = S3
endmodule

module REM2_s (
  input  B2,
  input  B1,
  input  B0,
  input  A2,
  input  A1,
  input  A0,
  input  Cin,
  output out_8,
  output out_9,
  output out_10,
  output out_11
);

  wire full_adder_2_cout, full_adder_3_cout, n7486_1__3__1y, n7486_1__6__2y, n7486_1__11__4y;

  Full_Adder full_adder_1 (.A(A2), .B(n7486_1__11__4y), .Cout(out_8), .Sum(out_9), .Cin(full_adder_2_cout));
  Full_Adder full_adder_2 (.A(A1), .B(n7486_1__6__2y), .Cout(full_adder_2_cout), .Sum(out_10), .Cin(full_adder_3_cout));
  Full_Adder full_adder_3 (.A(A0), .B(n7486_1__3__1y), .Cout(full_adder_3_cout), .Sum(out_11), .Cin(Cin));
  _7486 u_7486_1 (
    ._1__1A(B0), ._2__1B(Cin), ._3__1Y(n7486_1__3__1y), ._4__2A(Cin), ._5__2B(B1), ._6__2Y(n7486_1__6__2y),
    ._13__4B(B2), ._12__4A(Cin), ._11__4Y(n7486_1__11__4y));  // open: _7__GND, _14__Vcc, _10__3B, _9__3A, _8__3Y
endmodule
