// Logisim project Final final adder.circ as structural Verilog: 4 circuits, main circuit Final Adder/subtracor
module Final_Adder_subtracor (
  input  A3,
  input  A2,
  input  A1,
  input  A0,
  input  B3,
  input  B2,
  input  B1,
  input  B0,
  input  O,
  input  P,
  output S3,
  output S2,
  output S1,
  output S0,
  output Sign
);

  wire B_Sub, full_adder_1_sum, full_adder_2_cout, full_adder_2_sum, full_adder_3_cout, full_adder_3_sum,
       full_adder_4_cout, full_adder_4_sum, n2_s_comp_1_out_5, n2_s_comp_1_out_6, n2_s_comp_1_out_7,
       n2_s_comp_1_out_8, n7404_1__2__1y, n7404_1__4__2y, n7404_1__10__5y, n7404_1__12__6y, n7404_2__2__1y,
       n7404_2__12__6y, n7408_1__3__1y, n7408_1__8__3y, n7408_1__11__4y, n7408_2__11__4y, n7408_3__3__1y,
       n7432_1__11__4y, n7432_2__3__1y, n7432_2__6__2y, n7432_2__8__3y, n7432_2__11__4y, n7486_1__11__4y,
       n7486_2__3__1y, n7486_2__6__2y, Result;

  _7486 u_7486_1 (
    ._7__GND(1'b0), ._14__Vcc(1'b1), ._13__4B(A3), ._12__4A(Result), ._11__4Y(n7486_1__11__4y));  // open: _1__1A, _2__1B, _3__1Y, _4__2A, _5__2B, _6__2Y, _10__3B, _9__3A, _8__3Y
  _7432 u_7432_1 (
    ._7__GND(1'b0), ._14__Vcc(1'b1), ._13__4B(n7408_1__3__1y), ._12__4A(n7408_1__8__3y),
    ._11__4Y(n7432_1__11__4y));  // open: _1__1A, _2__1B, _3__1Y, _4__2A, _5__2B, _6__2Y, _10__3B, _9__3A, _8__3Y
  _7404 u_7404_1 (
    ._1__1A(Result), ._2__1Y(n7404_1__2__1y), ._3__2A(n7486_1__11__4y), ._4__2Y(n7404_1__4__2y),
    ._7__GND(1'b0), ._14__Vcc(1'b1), ._13__6A(A3), ._12__6Y(n7404_1__12__6y), ._11__5A(full_adder_1_sum),
    ._10__5Y(n7404_1__10__5y));  // open: _5__3A, _6__3Y, _9__4A, _8__4Y
  _7408 u_7408_1 (
    ._1__1A(n7404_1__10__5y), ._2__1B(n7486_1__11__4y), ._3__1Y(n7408_1__3__1y), ._4__2A(n7404_1__4__2y),
    ._5__2B(full_adder_1_sum), ._6__2Y(S3), ._14__Vcc(1'b1), ._13__4B(n7404_1__2__1y), ._12__4A(A3),
    ._11__4Y(n7408_1__11__4y), ._10__3B(Result), ._9__3A(A3), ._8__3Y(n7408_1__8__3y));  // open: _7__GND
  Full_Adder full_adder_1 (
    .A(n2_s_comp_1_out_5), .B(full_adder_2_cout), .Sum(full_adder_1_sum), .Cin(1'b0));  // open: Cout
  _7408 u_7408_2 (
    ._7__GND(1'b0), ._14__Vcc(1'b1), ._13__4B(n7404_2__2__1y), ._12__4A(n7404_2__12__6y),
    ._11__4Y(n7408_2__11__4y));  // open: _1__1A, _2__1B, _3__1Y, _4__2A, _5__2B, _6__2Y, _10__3B, _9__3A, _8__3Y
  Mux_2x1 mux_2x1_1 (.a(n7432_1__11__4y), .b(1'b0), .c(n7408_2__11__4y), .x(Sign));
  _2_s_Comp u_2_s_comp_1 (
    .in_1(A2), .in_2(A1), .in_3(A0), .out_5(n2_s_comp_1_out_5), .out_6(n2_s_comp_1_out_6),
    .out_7(n2_s_comp_1_out_7), .out_8(n2_s_comp_1_out_8), .Cin(n7408_1__11__4y));
  _7404 u_7404_2 (
    ._1__1A(n7432_2__6__2y), ._2__1Y(n7404_2__2__1y), ._7__GND(1'b0), ._14__Vcc(1'b1),
    ._13__6A(n7432_2__8__3y), ._12__6Y(n7404_2__12__6y));  // open: _3__2A, _4__2Y, _5__3A, _6__3Y, _11__5A, _10__5Y, _9__4A, _8__4Y
  Full_Adder full_adder_2 (
    .A(n2_s_comp_1_out_6), .B(B_Sub), .Cout(full_adder_2_cout), .Sum(full_adder_2_sum),
    .Cin(full_adder_3_cout));
  _7432 u_7432_2 (
    ._1__1A(A0), ._2__1B(A1), ._3__1Y(n7432_2__3__1y), ._4__2A(n7432_2__3__1y), ._5__2B(A2),
    ._6__2Y(n7432_2__6__2y), ._7__GND(1'b0), ._14__Vcc(1'b1), ._13__4B(B0), ._12__4A(B1),
    ._11__4Y(n7432_2__11__4y), ._10__3B(n7432_2__11__4y), ._9__3A(B2), ._8__3Y(n7432_2__8__3y));
  Full_Adder full_adder_3 (
    .A(n2_s_comp_1_out_7), .B(n7486_2__6__2y), .Cout(full_adder_3_cout), .Sum(full_adder_3_sum),
    .Cin(full_adder_4_cout));
  _2_s_Comp u_2_s_comp_2 (
    .in_1(full_adder_2_sum), .in_2(full_adder_3_sum), .in_3(full_adder_4_sum), .out_6(S2), .out_7(S1),
    .out_8(S0), .Cin(n7408_1__3__1y));  // open: out_5
  Full_Adder full_adder_4 (
    .A(n2_s_comp_1_out_8), .B(n7486_2__3__1y), .Cout(full_adder_4_cout), .Sum(full_adder_4_sum),
    .Cin(n7408_3__3__1y));
  _7486 u_7486_2 (
    ._1__1A(n7408_3__3__1y), ._2__1B(B0), ._3__1Y(n7486_2__3__1y), ._4__2A(n7408_3__3__1y), ._5__2B(B1),
    ._6__2Y(n7486_2__6__2y), ._7__GND(1'b0), ._14__Vcc(1'b1), ._13__4B(B3), ._12__4A(P), ._11__4Y(Result),
    ._10__3B(B2), ._9__3A(n7408_3__3__1y), ._8__3Y(B_Sub));
  _7408 u_7408_3 (
    ._1__1A(n7404_1__12__6y), ._2__1B(Result), ._3__1Y(n7408_3__3__1y), ._7__GND(1'b0), ._14__Vcc(1'b1));  // open: _4__2A, _5__2B, _6__2Y, _13__4B, _12__4A, _11__4Y, _10__3B, _9__3A, _8__3Y
endmodule

module Full_Adder (
  input  A,
  input  B,
  input  Cin,
  output Cout,
  output Sum
);

  wire n7408_1__3__1y, n7408_1__8__3y, n7408_1__11__4y, n7432_1__11__4y, n7486_1__3__1y;

  _7408 u_7408_1 (
    ._1__1A(B), ._2__1B(Cin), ._3__1Y(n7408_1__3__1y), ._7__GND(1'b0), ._14__Vcc(1'b1), ._13__4B(A),
    ._12__4A(B), ._11__4Y(n7408_1__11__4y), ._10__3B(A), ._9__3A(Cin), ._8__3Y(n7408_1__8__3y));  // open: _4__2A, _5__2B, _6__2Y
  _7432 u_7432_1 (
    ._7__GND(1'b0), ._14__Vcc(1'b1), ._13__4B(n7408_1__8__3y), ._12__4A(n7408_1__11__4y),
    ._11__4Y(n7432_1__11__4y), ._10__3B(n7432_1__11__4y), ._9__3A(n7408_1__3__1y), ._8__3Y(Cout));  // open: _1__1A, _2__1B, _3__1Y, _4__2A, _5__2B, _6__2Y
  _7486 u_7486_1 (
    ._1__1A(B), ._2__1B(Cin), ._3__1Y(n7486_1__3__1y), ._4__2A(n7486_1__3__1y), ._5__2B(A), ._6__2Y(Sum),
    ._7__GND(1'b0), ._14__Vcc(1'b1));  // open: _13__4B, _12__4A, _11__4Y, _10__3B, _9__3A, _8__3Y
endmodule

// 2's comp
module _2_s_Comp (
  input  in_1,
  input  in_2,
  input  in_3,
  input  Cin,
  output out_5,
  output out_6,
  output out_7,
  output out_8
);

  wire full_adder_2_cout, full_adder_3_cout, n7486_1__3__1y, n7486_1__6__2y, n7486_1__11__4y;

  Full_Adder full_adder_1 (.A(1'b0), .B(n7486_1__11__4y), .Cout(out_5), .Sum(out_6), .Cin(full_adder_2_cout));
  Full_Adder full_adder_2 (
    .A(1'b0), .B(n7486_1__6__2y), .Cout(full_adder_2_cout), .Sum(out_7), .Cin(full_adder_3_cout));
  Full_Adder full_adder_3 (.A(1'b0), .B(n7486_1__3__1y), .Cout(full_adder_3_cout), .Sum(out_8), .Cin(Cin));
  _7486 u_7486_1 (
    ._1__1A(in_3), ._2__1B(Cin), ._3__1Y(n7486_1__3__1y), ._4__2A(Cin), ._5__2B(in_2),
    ._6__2Y(n7486_1__6__2y), ._7__GND(1'b0), ._14__Vcc(1'b1), ._13__4B(in_1), ._12__4A(Cin),
    ._11__4Y(n7486_1__11__4y));  // open: _10__3B, _9__3A, _8__3Y
endmodule

module Mux_2x1 (
  input  a,
  input  b,
  input  c,
  output x
);

  wire n7404_1__2__1y, n7408_1__3__1y, n7408_1__6__2y;

  _7404 u_7404_1 (
    ._1__1A(c), ._2__1Y(n7404_1__2__1y), ._7__GND(1'b0), ._14__Vcc(1'b1));  // open: _3__2A, _4__2Y, _5__3A, _6__3Y, _13__6A, _12__6Y, _11__5A, _10__5Y, _9__4A, _8__4Y
  _7408 u_7408_1 (
    ._1__1A(b), ._2__1B(c), ._3__1Y(n7408_1__3__1y), ._4__2A(a), ._5__2B(n7404_1__2__1y),
    ._6__2Y(n7408_1__6__2y), ._7__GND(1'b0), ._14__Vcc(1'b1));  // open: _13__4B, _12__4A, _11__4Y, _10__3B, _9__3A, _8__3Y
  _7432 u_7432_1 (
    ._1__1A(n7408_1__3__1y), ._2__1B(n7408_1__6__2y), ._3__1Y(x), ._7__GND(1'b0), ._14__Vcc(1'b1));  // open: _4__2A, _5__2B, _6__2Y, _13__4B, _12__4A, _11__4Y, _10__3B, _9__3A, _8__3Y
endmodule
