// Logisim project FullAdder.circ as structural Verilog
module main (
  input  b,
  input  a,
  input  cin,
  output sum,
  output carry
);

  wire n7408_1__3__1y, n7408_1__6__2y, n7408_1__11__4y, n7432_1__3__1y, n7486_1__3__1y;

  _7432 u_7432_1 (
    ._1__1A(n7408_1__3__1y), ._2__1B(n7408_1__6__2y), ._3__1Y(n7432_1__3__1y), ._4__2A(n7432_1__3__1y),
    ._5__2B(n7408_1__11__4y), ._6__2Y(carry));  // open: _7__GND, _14__Vcc, _13__4B, _12__4A, _11__4Y, _10__3B, _9__3A, _8__3Y
  _7408 u_7408_1 (
    ._1__1A(a), ._2__1B(cin), ._3__1Y(n7408_1__3__1y), ._4__2A(a), ._5__2B(b), ._6__2Y(n7408_1__6__2y),
    ._13__4B(b), ._12__4A(cin), ._11__4Y(n7408_1__11__4y));  // open: _7__GND, _14__Vcc, _10__3B, _9__3A, _8__3Y
  _7486 u_7486_1 (
    ._1__1A(cin), ._2__1B(b), ._3__1Y(n7486_1__3__1y), ._4__2A(n7486_1__3__1y), ._5__2B(a), ._6__2Y(sum));  // open: _7__GND, _14__Vcc, _13__4B, _12__4A, _11__4Y, _10__3B, _9__3A, _8__3Y
endmodule

module FullAdder (
);

  main main_1 ();  // open: b, a, carry, sum, cin
endmodule
