// Logisim project Integration.circ as structural Verilog: 1 circuit, main circuit Integration
module Integration (
  input  sign_1,
  input  a0,
  input  a1,
  input  a2,
  input  sign_2,
  input  b0,
  input  b1,
  input  b2,
  input  O,
  input  P,
  output divide_by_zero,
  output add_zero_flag,
  output mult_zero_flag
);

  wire alu_1_s0, alu_1_s1, alu_1_s2, alu_1_s3, alu_1_s4, alu_1_s5, alu_1_sign, at, au, bt, bu, ct, cu, dt,
       du, et, eu, ft, fu, gt, gu, sign;

  BCD_to_7_segment bcd_to_7_segment_1 (
    .et(et), .sign(alu_1_sign), .dt(dt), .ct(ct), .a5(alu_1_s5), .a4(alu_1_s4), .a3(alu_1_s3), .eu(eu),
    .a2(alu_1_s2), .du(du), .a1(alu_1_s1), .cu(cu), .a0(alu_1_s0), .sign_2(sign), .gt(gt), .ft(ft), .at(at),
    .bt(bt), .gu(gu), .fu(fu), .au(au), .bu(bu));
  ALU alu_1 (
    .sign1(sign_1), .a0(a0), .a1(a1), .a2(a2), .sign2(sign_2), .b0(b0), .b1(b1), .b2(b2), .O(O), .P(P),
    .add_sub_zero_flag(add_zero_flag), .mult_zero_flag(mult_zero_flag), .S4(alu_1_s4), .S2(alu_1_s2),
    .S0(alu_1_s0), .sign(alu_1_sign), .S5(alu_1_s5), .S1(alu_1_s1), .S3(alu_1_s3), .out_17(divide_by_zero));
  _7_Segment_Display u_7_segment_display_1 (.g(sign));  // open: f, a, b, e, d, c, dp
  _7_Segment_Display u_7_segment_display_2 (.g(gt), .f(ft), .a(at), .b(bt), .e(et), .d(dt), .c(ct));  // open: dp
  _7_Segment_Display u_7_segment_display_3 (.g(gu), .f(fu), .a(au), .b(bu), .e(eu), .d(du), .c(cu));  // open: dp
endmodule
