// Logisim project MultiplierFINAL.circ as structural Verilog: 3 circuits, main circuit Multiplier
module Multiplier (
  input  A0,
  input  B0,
  input  A1,
  input  B1,
  input  A2,
  input  B2,
  input  A3,
  input  B3,
  output O1,
  output O2,
  output O3,
  output O4,
  output O5,
  output O6,
  output O7
);

  wire full_adder_1_carry, full_adder_2_carry, full_adder_2_sum, full_adder_3_carry, full_adder_3_sum,
       full_adder_4_carry, full_adder_5_carry, n7404_1__2__1y, n7404_1__4__2y, n7404_1__6__3y,
       n7408_1__3__1y, n7408_2__6__2y, n7408_2__8__3y, n7408_2__11__4y, n7408_3__3__1y, n7408_3__6__2y,
       n7408_3__8__3y, n7408_3__11__4y, n7432_1__3__1y, n7432_2__3__1y, n7432_2__6__2y, n7432_2__8__3y,
       n7432_2__11__4y, n7486_1__3__1y;

  _7404 u_7404_1 (
    ._1__1A(n7432_2__6__2y), ._2__1Y(n7404_1__2__1y), ._3__2A(n7432_2__8__3y), ._4__2Y(n7404_1__4__2y),
    ._5__3A(n7432_1__3__1y), ._6__3Y(n7404_1__6__3y), ._7__GND(1'b0), ._14__Vcc(1'b1));  // open: _13__6A, _12__6Y, _11__5A, _10__5Y, _9__4A, _8__4Y
  _7432 u_7432_1 (
    ._1__1A(n7404_1__2__1y), ._2__1B(n7404_1__4__2y), ._3__1Y(n7432_1__3__1y), ._7__GND(1'b0));  // open: _4__2A, _5__2B, _6__2Y, _14__Vcc, _13__4B, _12__4A, _11__4Y, _10__3B, _9__3A, _8__3Y
  _7408 u_7408_1 (
    ._1__1A(A2), ._2__1B(B2), ._3__1Y(n7408_1__3__1y), ._4__2A(n7404_1__6__3y), ._5__2B(n7486_1__3__1y),
    ._6__2Y(O7), ._7__GND(1'b0), ._14__Vcc(1'b1));  // open: _13__4B, _12__4A, _11__4Y, _10__3B, _9__3A, _8__3Y
  _7408 u_7408_2 (
    ._1__1A(A0), ._2__1B(B0), ._3__1Y(O1), ._4__2A(B0), ._5__2B(A1), ._6__2Y(n7408_2__6__2y), ._7__GND(1'b0),
    ._14__Vcc(1'b1), ._13__4B(A0), ._12__4A(B1), ._11__4Y(n7408_2__11__4y), ._10__3B(A2), ._9__3A(B0),
    ._8__3Y(n7408_2__8__3y));
  _7408 u_7408_3 (
    ._1__1A(A1), ._2__1B(B1), ._3__1Y(n7408_3__3__1y), ._4__2A(A2), ._5__2B(B1), ._6__2Y(n7408_3__6__2y),
    ._7__GND(1'b0), ._14__Vcc(1'b1), ._13__4B(A0), ._12__4A(B2), ._11__4Y(n7408_3__11__4y), ._10__3B(A1),
    ._9__3A(B2), ._8__3Y(n7408_3__8__3y));
  _7486 u_7486_1 (
    ._1__1A(A3), ._2__1B(B3), ._3__1Y(n7486_1__3__1y), ._7__GND(1'b0), ._14__Vcc(1'b1));  // open: _4__2A, _5__2B, _6__2Y, _13__4B, _12__4A, _11__4Y, _10__3B, _9__3A, _8__3Y
  full_adder full_adder_1 (.b(n7408_2__11__4y), .a(n7408_2__6__2y), .carry(full_adder_1_carry), .sum(O2), .cin(1'b0));
  full_adder full_adder_2 (
    .b(n7408_3__3__1y), .a(n7408_2__8__3y), .carry(full_adder_2_carry), .sum(full_adder_2_sum),
    .cin(full_adder_1_carry));
  full_adder full_adder_3 (
    .b(n7408_3__6__2y), .a(1'b0), .carry(full_adder_3_carry), .sum(full_adder_3_sum), .cin(full_adder_2_carry));
  _7432 u_7432_2 (
    ._1__1A(A0), ._2__1B(A1), ._3__1Y(n7432_2__3__1y), ._4__2A(n7432_2__3__1y), ._5__2B(A2),
    ._6__2Y(n7432_2__6__2y), ._7__GND(1'b0), ._14__Vcc(1'b1), ._13__4B(B0), ._12__4A(B1),
    ._11__4Y(n7432_2__11__4y), ._10__3B(n7432_2__11__4y), ._9__3A(B2), ._8__3Y(n7432_2__8__3y));
  full_adder full_adder_4 (.b(n7408_3__11__4y), .a(full_adder_2_sum), .carry(full_adder_4_carry), .sum(O3), .cin(1'b0));
  full_adder full_adder_5 (
    .b(n7408_3__8__3y), .a(full_adder_3_sum), .carry(full_adder_5_carry), .sum(O4), .cin(full_adder_4_carry));
  full_adder full_adder_6 (.b(n7408_1__3__1y), .a(full_adder_3_carry), .carry(O6), .sum(O5), .cin(full_adder_5_carry));
endmodule

// Adder
module _3_Bit_full_adder (
  input  Carry,
  input  A,
  input  B,
  input  C,
  output S,
  output C_2
);

  wire n7408_1__3__1y, n7408_2__3__1y, n7408_2__6__2y, n7408_2__8__3y, n7408_2__11__4y, n7432_1__3__1y,
       n7432_1__6__2y, n7486_1__3__1y, n7486_1__6__2y;

  _7408 u_7408_1 (
    ._1__1A(C), ._2__1B(Carry), ._3__1Y(n7408_1__3__1y));  // open: _4__2A, _5__2B, _6__2Y, _7__GND, _14__Vcc, _13__4B, _12__4A, _11__4Y, _10__3B, _9__3A, _8__3Y
  _7408 u_7408_2 (
    ._1__1A(A), ._2__1B(B), ._3__1Y(n7408_2__3__1y), ._4__2A(n7408_2__3__1y), ._5__2B(C),
    ._6__2Y(n7408_2__6__2y), ._13__4B(A), ._12__4A(Carry), ._11__4Y(n7408_2__11__4y), ._10__3B(B),
    ._9__3A(Carry), ._8__3Y(n7408_2__8__3y));  // open: _7__GND, _14__Vcc
  _7486 u_7486_1 (
    ._1__1A(A), ._2__1B(B), ._3__1Y(n7486_1__3__1y), ._4__2A(n7486_1__3__1y), ._5__2B(C),
    ._6__2Y(n7486_1__6__2y), ._13__4B(n7486_1__6__2y), ._12__4A(Carry), ._11__4Y(S));  // open: _7__GND, _14__Vcc, _10__3B, _9__3A, _8__3Y
  _7432 u_7432_1 (
    ._1__1A(n7408_2__6__2y), ._2__1B(n7408_2__11__4y), ._3__1Y(n7432_1__3__1y), ._4__2A(n7432_1__3__1y),
    ._5__2B(n7408_2__8__3y), ._6__2Y(n7432_1__6__2y), ._10__3B(n7432_1__6__2y), ._9__3A(n7408_1__3__1y),
    ._8__3Y(C_2));  // open: _7__GND, _14__Vcc, _13__4B, _12__4A, _11__4Y
endmodule

module full_adder (
  input  b,
  input  a,
  input  cin,
  output sum,
  output carry
);

  wire n7408_1__3__1y, n7408_1__6__2y, n7408_1__11__4y, n7432_1__3__1y, n7486_1__3__1y;

  _7432 u_7432_1 (
    ._1__1A(n7408_1__3__1y), ._2__1B(n7408_1__6__2y), ._3__1Y(n7432_1__3__1y), ._4__2A(n7432_1__3__1y),
    ._5__2B(n7408_1__11__4y), ._6__2Y(carry));  // open: _7__GND, _14__Vcc, _13__4B, _12__4A, _11__4Y, _10__3B, _9__3A, _8__3Y
  _7408 u_7408_1 (
    ._1__1A(a), ._2__1B(cin), ._3__1Y(n7408_1__3__1y), ._4__2A(a), ._5__2B(b), ._6__2Y(n7408_1__6__2y),
    ._13__4B(b), ._12__4A(cin), ._11__4Y(n7408_1__11__4y));  // open: _7__GND, _14__Vcc, _10__3B, _9__3A, _8__3Y
  _7486 u_7486_1 (
    ._1__1A(cin), ._2__1B(b), ._3__1Y(n7486_1__3__1y), ._4__2A(n7486_1__3__1y), ._5__2B(a), ._6__2Y(sum));  // open: _7__GND, _14__Vcc, _13__4B, _12__4A, _11__4Y, _10__3B, _9__3A, _8__3Y
endmodule
